# Fritzing sketch Composite (saved by Fritzing 0.8.7b)
breadboards: 1

parts:
  R1 = Resistor [tolerance=±10% resistance=470 package=THT]
  R2 = Resistor [tolerance=±10% resistance=1k package=THT]

nets:
  Espruino A7: R1.Pin_0
  RCA Signal: R1.Pin_1, R2.Pin_1
  Espruino A6: R2.Pin_0
