# Fritzing sketch VGA (saved by Fritzing 0.8.7b)
breadboards: 1

parts:
  R1 = Resistor [tolerance=±10% resistance=330 package=THT]
  R2 = Resistor [tolerance=±10% resistance=330 package=THT]
  R3 = Resistor [tolerance=±10% resistance=330 package=THT]
  R4 = Resistor [tolerance=±10% resistance=100 package=THT]
  R5 = Resistor [tolerance=±10% resistance=100 package=THT]
  R6 = Resistor [tolerance=±10% resistance=100 package=THT]

nets:
  Espruino A7: R1.Pin_0
  VGA Pins 1,2 and 3 (R,G and B): R1.Pin_1, R4.Pin_0
  Espruino A6: R2.Pin_0
  VGA Pin 13 (HSYNC): R2.Pin_1, R5.Pin_0
  Espruino A5: R3.Pin_0
  VGA Pin 14 (VSYNC): R3.Pin_1, R6.Pin_0
  Espruino GND/VGA Pins 5,6,7,8,9,10 (GND): R4.Pin_1, R5.Pin_1, R6.Pin_1
